# Fritzing sketch circuit diagram (saved by Fritzing 0.9.5d)

parts:
  HC-SR04_Sensor_1 = HC-SR04 Ultrasonic Distance Sensor
  VCC1 = Battery
  J1 = Piezo Speaker
  Part2 = Arduino Nano (Rev3.0)
  S1 = Toggle Switch [package=THT]

nets:
  VCC: HC-SR04_Sensor_1.VCC, Part2.5V
  N1: HC-SR04_Sensor_1.TRIG, Part2.D9
  N2: HC-SR04_Sensor_1.ECHO, Part2.D10
  GND: HC-SR04_Sensor_1.GND, VCC1.-, Part2.GND
  N3: J1.pin2, Part2.D8
  N4: Part2.VIN, S1.L1
